// Logisim project EIE348_2025-01_4bitadder.circ as structural Verilog: 1 circuit, main circuit main
module main (
);

  wire adder_1_cout, adder_1_out, adder_2_cout, adder_2_out, adder_3_cout, adder_3_out, adder_4_cout,
       adder_4_out, dipswitch_1_p1, dipswitch_1_p2, dipswitch_1_p3, dipswitch_1_p4, dipswitch_2_p1,
       dipswitch_2_p2, dipswitch_2_p3, dipswitch_2_p4;

  // DipSwitch dipswitch_1: pin names not known; wires that end beside it: dipswitch_1_p1, dipswitch_1_p2, dipswitch_1_p3, dipswitch_1_p4
  // DipSwitch dipswitch_2: pin names not known; wires that end beside it: dipswitch_2_p1, dipswitch_2_p2, dipswitch_2_p3, dipswitch_2_p4
  LED led_1 (.in(adder_4_cout));
  Adder #(.width(1)) adder_1 (
    .a(dipswitch_1_p1), .b(dipswitch_2_p1), .out(adder_1_out), .cin(1'b0), .cout(adder_1_cout));
  LED led_2 (.in(adder_1_out));
  Adder #(.width(1)) adder_2 (
    .a(dipswitch_1_p2), .b(dipswitch_2_p2), .out(adder_2_out), .cin(adder_1_cout), .cout(adder_2_cout));
  LED led_3 (.in(adder_2_out));
  Adder #(.width(1)) adder_3 (
    .a(dipswitch_1_p3), .b(dipswitch_2_p3), .out(adder_3_out), .cin(adder_2_cout), .cout(adder_3_cout));
  LED led_4 (.in(adder_3_out));
  Adder #(.width(1)) adder_4 (
    .a(dipswitch_1_p4), .b(dipswitch_2_p4), .out(adder_4_out), .cin(adder_3_cout), .cout(adder_4_cout));
  LED led_5 (.in(adder_4_out));

  // Notes on the sheet:
  //   Palabra de 4 bits A
  //   Palabra de 4 bits B
  //   EIE348-2025-02 - Prof. Jorge Marin - PUCV
  //   Sumador de 4 bits usando 4 full adders
  //   --> La palabra de 4 bits A se suma con la palabra de 4 bits B (definidas por los switches DIP)
  //   --> El resultado se despliega en la palabra de 4 bits Y más un carry Cy desplegada por los LEDs
  //   Y0
  //   Y1
  //   Y2
  //   Y3
  //   CY
  //   Carry de salida CY
  //   Palabra de 4 bits Y = Y3|Y2|Y1|Y0
endmodule
