// Logisim project EIE348_2025-01_FSM_T8P2p1_example.circ as structural Verilog: 1 circuit, main circuit main
module main (
  input  Entrada_A,
  input  in_2
);

  wire and_1_out, clock_1_out, d_ff_1_q, d_ff_2_q, not_1_out;

  and and_1 (and_1_out, d_ff_2_q, Entrada_A);
  not not_1 (not_1_out, Entrada_A);
  D_Flip_Flop d_ff_1 (.D(and_1_out), .clk(clock_1_out), .Q(d_ff_1_q), .reset(in_2));  // open: Qn, preset
  D_Flip_Flop d_ff_2 (.D(not_1_out), .clk(clock_1_out), .Q(d_ff_2_q), .reset(in_2));  // open: Qn, preset
  Clock clock_1 (.out(clock_1_out));
  LED led_1 (.in(d_ff_1_q));

  // Notes on the sheet:
  //   Salida Y
endmodule
