// Logisim project EIE348_2025-01_SRlatches.circ as structural Verilog: 1 circuit, main circuit main
module main (
);

  wire button_1_out, button_2_out, button_3_out, button_4_out, button_5_out, nand_1_out, nand_2_out,
       nand_3_out, nand_4_out, nor_1_out, nor_2_out, nor_3_out, nor_4_out, not_1_out;

  Button #(.press("passive")) button_1 (.out(button_1_out));
  Button #(.press("passive")) button_2 (.out(button_2_out));
  Button button_3 (.out(button_3_out));
  Button button_4 (.out(button_4_out));
  nor nor_1 (nor_1_out, button_3_out, nor_2_out);
  nor nor_2 (nor_2_out, nor_1_out, button_4_out);
  nand nand_1 (nand_1_out, button_1_out, nand_2_out);
  nand nand_2 (nand_2_out, nand_1_out, button_2_out);
  LED led_1 (.in(nor_1_out));
  LED led_2 (.in(nor_2_out));
  LED led_3 (.in(nand_1_out));
  LED led_4 (.in(nand_2_out));
  Button button_5 (.out(button_5_out));
  not not_1 (not_1_out, button_5_out);
  nand nand_3 (nand_3_out, button_5_out, 1'b1);
  nand nand_4 (nand_4_out, 1'b1, not_1_out);
  nor nor_3 (nor_3_out, nand_3_out, nor_4_out);
  nor nor_4 (nor_4_out, nor_3_out, nand_4_out);
  LED led_5 (.in(nor_3_out));
  LED led_6 (.in(nor_4_out));

  // Notes on the sheet:
  //   RESET
  //   SET
  //   SET
  //   RESET
  //   EIE348-2025-02 - Prof. Jorge Marin - PUCV
  //   Latches SR activos a nivel ALTO (arriba) y a nivel BAJO (abajo)
  //   NOTA: los botones del latch de abajo están activados por defecto, y al presionarlos entregan valor 0
  //   Q
  //   Q'
  //   Q
  //   Q'
endmodule
