// Logisim project EIE348_2025-01_bin_to_7seg.circ as structural Verilog: 1 circuit, main circuit main
module main (
);

  wire bcd_to_7_segment_decoder_1_p1, bcd_to_7_segment_decoder_2_p1;
  wire [3:0] binary_to_bcd_converter_1_p4;
  wire [7:0] dipswitch_1_sw1;

  DipSwitch dipswitch_1 (
    .sw1(dipswitch_1_sw1[0]), .sw2(dipswitch_1_sw1[1]), .sw3(dipswitch_1_sw1[2]), .sw4(dipswitch_1_sw1[3]),
    .sw5(dipswitch_1_sw1[4]), .sw6(dipswitch_1_sw1[5]), .sw7(dipswitch_1_sw1[6]), .sw8(dipswitch_1_sw1[7]));
  _7_Segment_Display u_7_segment_display_1 ();  // open: g, f, a, b, e, d, c, dp
  // BCD_to_7_Segment_decoder bcd_to_7_segment_decoder_1: pin names not known; wires that end beside it: bcd_to_7_segment_decoder_1_p1
  _7_Segment_Display u_7_segment_display_2 ();  // open: g, f, a, b, e, d, c, dp
  // BCD_to_7_Segment_decoder bcd_to_7_segment_decoder_2: pin names not known; wires that end beside it: bcd_to_7_segment_decoder_2_p1
  // Binary_to_BCD_converter binary_to_bcd_converter_1: pin names not known; wires that end beside it: {1'b0, dipswitch_1_sw1}, bcd_to_7_segment_decoder_1_p1, bcd_to_7_segment_decoder_2_p1, binary_to_bcd_converter_1_p4
  _7_Segment_Display u_7_segment_display_3 ();  // open: g, f, a, b, e, d, c, dp
  // BCD_to_7_Segment_decoder bcd_to_7_segment_decoder_3: pin names not known; wires that end beside it: binary_to_bcd_converter_1_p4
  LED led_1 (.in(binary_to_bcd_converter_1_p4[0]));
  LED led_2 (.in(binary_to_bcd_converter_1_p4[1]));
  LED led_3 (.in(binary_to_bcd_converter_1_p4[2]));
  LED led_4 (.in(binary_to_bcd_converter_1_p4[3]));

  // Notes on the sheet:
  //   Codificador binario-7 segmentos
  //   EIE348-2025-02 - Prof. Jorge Marin - PUCV
  //   Palabra binaria de entrada (de izquierda a derecha)
  //   --> La palabra de 8 bits de entrada (definidas por los switches DIP) de codifica a BCD
  //   --> El resultado se despliega en los displays de 7 segmentos (y en los LEDS como binario para el dígito de la derecha)
  //   D1_0
  //   D1_1
  //   D1_2
  //   D1_3
  //   D1_3|D1_2|D1_1|D1_0
  //   Palabra de 4 bits (dígito decimal menos significativo)
endmodule
